// Digital circuit baby8_control.dig as structural Verilog
module baby8_control (
  input  [7:0] dIn,
  input  Z,
  input  C,
  input  N,
  input  V,
  input  clock,
  input  resetn,
  input  \int ,
  output wReg,
  output [3:0] wAd,
  output [3:0] aAd,
  output [3:0] bAd,
  output [1:0] bSel,
  output [1:0] logSel,
  output [1:0] aSel,
  output Cin,
  output A7,
  output A0,
  output a7S,
  output a0S,
  output wMem,
  output out3,
  output out2,
  output out1,
  output out0,
  output rMem
);

  Register #(.Bits(8)) IR (.D(dIn), .C(clock));  // open: en, Q
  Register #(.Bits(4)) flags (.D({V, N, C, Z}), .C(clock));  // open: en, Q

  // Notes on the sheet:
  //   dIn: data from external memory
  //   Z: zero flag from ALU
  //   C: carry flag from ALU
  //   N: negative flag from ALU
  //   V: overflow flag from ALU
  //   clock: system clock
  //   resetn: resets system when low
  //   int: interrupt when high
  //   wReg: writes the selected register
  //   wAd: register to write
  //   aAd: register to read for second operand
  //   bAd: register to read for first operand
  //   bSel: use register, memory or i/o as operand
  //   logSel: logical operation
  //   aSel: normal, inverted or constant
  //   Cin: output carry in for ALU
  //   A7: replacement value for A7
  //   A0: replacement value for A0
  //   a7S: use alternative A7
  //   a0S: use alternative A0
  //   wMem: asks memory to save data
  //   out3: output port 3 should load dOut
  //   out2: output port 2 should load dOut
  //   out1: output port 1 should load dOut
  //   out0: output port 0 should load dOut
  //   rMem: asks memory to output data
endmodule
