// Digital circuit baby8_datapath.dig as structural Verilog
// This simple circuit can do all the operations needed to execute Baby8 instructions
module baby8_datapath (
  input  clock,
  input  [7:0] in0,
  input  [7:0] in1,
  input  wReg,
  input  [3:0] wAd,
  input  [3:0] aAd,
  input  [3:0] bAd,
  input  [7:0] dIn,
  input  [1:0] bSel,
  input  [1:0] logSel,
  input  Cin,
  input  A7,
  input  A0,
  input  a7S,
  input  a0S,
  input  [1:0] aSel,
  output [7:0] dOut,
  output [15:0] address,
  output Z,
  output V,
  output N,
  output C
);

  wire [7:0] baby8_alu_1_r, multiplexer_1_out, registers_db;

  RegisterFile #(.AddrBits(4), .Bits(8)) registers (
    .Din(baby8_alu_1_r), .we(wReg), .Rw(wAd), .C(clock), .Ra(aAd), .Rb(bAd), .Da(address[15:8]),
    .Db({registers_db[7], address[6:1], registers_db[0]}));
  Multiplexer #(.Selector_Bits(2), .Bits(8)) multiplexer_1 (
    .sel(bSel), .in_0({registers_db[7], address[6:1], registers_db[0]}), .in_1(dIn), .in_2(in0), .in_3(in1),
    .out(multiplexer_1_out));
  baby8_alu baby8_alu_1 (
    .R(baby8_alu_1_r), .logSel(logSel), .aSel(aSel), .C(C), .Cin(Cin), .A(address[15:8]),
    .B(multiplexer_1_out), .Z(Z), .N(N), .V(V));
  Multiplexer multiplexer_2 (.sel(a7S), .in_0(registers_db[7]), .in_1(A7), .out(address[7]));
  Multiplexer multiplexer_3 (.sel(a0S), .in_0(registers_db[0]), .in_1(A0), .out(address[0]));
  Register #(.Bits(8)) prevR (.D(baby8_alu_1_r), .C(clock), .en(1'b1), .Q(dOut));

  // Notes on the sheet:
  //   clock: all registers store their inputs (when enabled) at the rising edge of this signal
  //   in0: input port at address 0
  //   in1: input port at address 1
  //   wReg: allow register selected by adW to receive the value from R
  //   wAd: register to be written
  //   aAd: register to use for A
  //   bAd: register to use for B
  //   dOut: result of the addition in the previous cycle - used as data to be written to main memory
  //   dIn: value read from main memory
  //   address: address for main memory
  //   bSel: select register, memory or input port for B
  //   logSel: select logical operation between A and B or just use B
  //   Z: addition had zero result
  //   Cin: carry in
  //   A7: replacement for A7
  //   A0: replacement for A0
  //   a7S: use original A7 or replacement
  //   a0S: use original A0 or replacement
  //   aSel: operand A or constant
  //   V: overflow - result has different sign from operands
  //   N: negative result
  //   C: carry out
  //   Address Modification
endmodule
