// Digital circuit fsm2control.dig as structural Verilog
// converts the encoded outputs from the Finite State Machine into the actual
// values used by the datapath
module fsm2control (
  input  [3:0] wAdIn,
  input  [3:0] aAdIn,
  input  [3:0] bAdIn,
  input  [1:0] bSelfIn,
  input  [1:0] logSelIn,
  input  [1:0] aSelIn,
  input  [1:0] CinIn,
  input  [3:0] \reg ,
  input  [1:0] svD,
  output [3:0] wAd,
  output [3:0] aAd,
  output [3:0] bAd,
  output [1:0] bSel,
  output [1:0] logSel,
  output [1:0] aSel,
  output Cin,
  output out3,
  output out2,
  output out1,
  output out0
);

  wire or_1_out;
  wire [1:0] or_2_out;
  wire [2:2] xor_1_out;

  buf xor_1 (xor_1_out[2], wAdIn[2]);  // XOr open: In_1
  or or_1 (or_1_out, wAdIn[2], wAdIn[3]);
  or or_2 (or_2_out[0], wAdIn[0], or_1_out);
  or or_3 (or_2_out[1], wAdIn[1], or_1_out);
  Multiplexer #(.Bits(4), .Selector_Bits(2)) multiplexer_1 (
    .sel(or_2_out), .in_0(\reg ), .in_1({2'b00, svD}), .in_3({wAdIn[3], xor_1_out[2], wAdIn[1:0]}), .out(wAd));  // open: in_2

  // Notes on the sheet:
  //   wAd: register to write
  //   aAd: register to read for second operand
  //   bAd: register to read for first operand
  //   bSel: use register, memory or i/o as operand
  //   logSel: logical operation
  //   aSel: normal, inverted or constant
  //   Cin: output carry in for ALU
  //   out3: output port 3 should load dOut
  //   out2: output port 2 should load dOut
  //   out1: output port 1 should load dOut
  //   out0: output port 0 should load dOut
  //   wAdIn: raw address for register to write
  //   aAdIn: raw address for first operand
  //   bAdIn: raw address for second operand
  //   bSelfIn: raw selection of second operand
  //   logSelIn: raw selection of logic operation
  //   aSelIn: raw selection of first operand
  //   CinIn: raw selection of carry in calculation
  //   reg: low 4 bits of zero page address
  //   svD: saved bit of destination in instruction
endmodule
